# Fritzing sketch Demo (saved by Fritzing 0.9.10b)
breadboards: 1

parts:
  U1 = 555 Timer [package="DIP8 [THT]"]
  R3 = Resistor [tolerance=±5% power=0.25 resistance=330 package=THT]
  LED1 = LED - 5mm [color="Blue (430nm)" current=0.030 package="5 mm [THT]"]
  C1 = Electrolytic Capacitor [capacitance=1µF voltage=35V package="100 mil [THT, electrolytic]"]
  BAT1 = Battery Holders [package=battcom_20mm_pth]
  R2 = Resistor [tolerance=±5% power=0.25 resistance=7.5k package=THT]
  R1 = Resistor [tolerance=±5% power=0.25 resistance=7.5k package=THT]

nets:
  N1: U1.Ground, LED1.anode, C1.-, BAT1.-
  N2: U1.Trigger, U1.Threshold, C1.+, R2.Pin_0
  N3: U1.Output, R3.Pin_0
  N4: U1.Reset, U1.Vcc_Supply_Voltage, BAT1.+, R1.Pin_0
  N5: U1.Discharge, R2.Pin_1, R1.Pin_1
  N6: R3.Pin_1, LED1.cathode
